# Fritzing sketch rfm69hcw-wiring (saved by Fritzing 0.9.3b)

parts:
  Part1 = Adafruit RFM69HCW Transceiver Radio [part_number="Adafruit #3070 and #3071"]
  Part2 = Adafruit Radio FeatherWing [part_number="Adafruit #3229, 3230, 3231, 3232"]
  Mod1 = Raspberry Pi Pico W

nets:
  N1: Part1.DIO2, Part1.DIO3, Part1.DIO4, Mod1.pin_15
  N2: Part1.VIN, Mod1.pin_34, Mod1.pin_35, Mod1.pin_36
  N3: Part1.GND, Part1.EN, Part1.DIO0, Mod1.pin_7, Mod1.pin_8, Mod1.pin_18, Mod1.pin_42
  N4: Part1.SCK, Mod1.pin_24
  N5: Part1.MISO, Mod1.pin_21
  N6: Part1.MOSI, Mod1.pin_25
  N7: Part1.CS, Mod1.pin_9
  N8: Part1.RST, Mod1.pin_12
  N9: Part2.DIO2, Part2.A
  N10: Part2.IRQ, Part2.E
  N11: Part2.CS, Part2.D
  N12: Part2.RF_RST, Part2.C

notes:
  A: GPIO11 - DIO2 / G2
  C: GPIO9 - RST / Reset
  D: GPIO6 - CS / NSS
  E: GPIO5 - DIO0 / G0 / IRQ

custom parts:
  Adafruit RFM69HCW Transceiver Radio: Sending data over long distances is like magic, and now you can be a magician with this range of powerful and easy-to-use radio modules. Sure, sometimes you want to talk to a computer (a good time to use WiFi) or perhaps communicate with a Phone (choose Bluetooth Low Energy!) but what if you want to send data very far? Most WiFi, Bluetooth, Zigbee and other wireless chipsets use 2.4GHz, which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
  Adafruit Radio FeatherWing: Add short-hop wireless to your Feather with these Radio Featherwings. These add-ons for any Feather board will let you integrate packetized radio (with the RFM69 radio) or LoRa radio (with the RFM9x's). These radios are good options for kilometer-range radio, and paired with one of our WiFi, cellular or Bluetooth Feathers, will let you bridge from 433/900 MHz to the Internet or your mobile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
  Raspberry Pi Pico W: Raspberry Pi Pico W. Based around the RP2040 microcontroller the Pico W is a low cost microcontroller device bringing Raspberry Pi quality, cost, and easy of use to the microcontroller space. The areas marked KEEPOUT in pcb silkscreen should not have traces running through them to avoid shorts on a soldered in module!
